# Fritzing sketch smartoled (saved by Fritzing 0.9.3b)
breadboards: 1

parts:
  WeMos_D1_Mini1 = WeMos D1 Mini
  128x64_SSD1306_0_96"_OLED_Display = Grove OLED 128x96
  TTP223_Capacitive_button = IR Receiver Breakout [package=PCB]

nets:
  3V3: WeMos_D1_Mini1.3V3, TTP223_Capacitive_button.VCC
  5V: WeMos_D1_Mini1.5V, 128x64_SSD1306_0_96"_OLED_Display.VCC
  N1: WeMos_D1_Mini1.D1, 128x64_SSD1306_0_96"_OLED_Display.SCL
  N2: WeMos_D1_Mini1.D2, 128x64_SSD1306_0_96"_OLED_Display.SDA
  N3: WeMos_D1_Mini1.D5, TTP223_Capacitive_button.OUT
  GND: WeMos_D1_Mini1.G, 128x64_SSD1306_0_96"_OLED_Display.GND, TTP223_Capacitive_button.GND

notes:
  Davide Perini
  SmartOled
  MQTT Broker Display
