# Fritzing sketch smartostat (saved by Fritzing 0.9.3b)

parts:
  WeMos_D1_Mini1 = WeMos D1 Mini
  WeMos_D1_Mini_Relay_Shield_V1_PIN_D5 = WeMos D1 Mini Relay Shield V2
  SR-501_PIR = HC-SR501 Body Sensor Module
  OLED_D6_Touch_Button = IR Receiver Breakout [package=PCB]
  Furnance_D8_Touch_Button = IR Receiver Breakout [package=PCB]
  SSD1306_0_96"_OLED_Display_128x64_pixel = Grove OLED 128x96
  WeMos_D1_Mini_Dual_Base_Shield1 = WeMos D1 Mini Dual Base Shield  # not connected
  Lolin_IR_Shield = WeMos D1 Mini Protoboard Shield
  IR1 = TSOP312.., 314.. [package=THT]
  LED1 = LED - 5mm [color="Red (633nm)" package="5 mm [THT]"]
  Bosch_BME680_Environmental_Sensor_(temp_humidity_pressure_air_quality) = Adafruit BME680
  1000uf_capacitor = Capacitor Polarized [package=nippon_f80]

nets:
  3V3: WeMos_D1_Mini1.3V3, Bosch_BME680_Environmental_Sensor_(temp_humidity_pressure_air_quality).VIN
  5V: WeMos_D1_Mini1.5V, OLED_D6_Touch_Button.VCC
  N1: WeMos_D1_Mini1.D1, Bosch_BME680_Environmental_Sensor_(temp_humidity_pressure_air_quality).SCK/SCL
  N2: WeMos_D1_Mini1.D2, Bosch_BME680_Environmental_Sensor_(temp_humidity_pressure_air_quality).SDI/SDA
  N3: WeMos_D1_Mini1.D5, SR-501_PIR.OUT
  N4: WeMos_D1_Mini1.D6, OLED_D6_Touch_Button.OUT
  GND: WeMos_D1_Mini1.G, OLED_D6_Touch_Button.GND, Bosch_BME680_Environmental_Sensor_(temp_humidity_pressure_air_quality).GND, Bosch_BME680_Environmental_Sensor_(temp_humidity_pressure_air_quality).SDO/ADR
  3V3_2: WeMos_D1_Mini_Relay_Shield_V1_PIN_D5.3V3, Lolin_IR_Shield.3V3
  5V_2: WeMos_D1_Mini_Relay_Shield_V1_PIN_D5.5V, SSD1306_0_96"_OLED_Display_128x64_pixel.VCC, 1000uf_capacitor.+
  N5: WeMos_D1_Mini_Relay_Shield_V1_PIN_D5.D1, SSD1306_0_96"_OLED_Display_128x64_pixel.SCL
  N6: WeMos_D1_Mini_Relay_Shield_V1_PIN_D5.D2, SSD1306_0_96"_OLED_Display_128x64_pixel.SDA
  N7: WeMos_D1_Mini_Relay_Shield_V1_PIN_D5.D3, Lolin_IR_Shield.D3
  N8: WeMos_D1_Mini_Relay_Shield_V1_PIN_D5.D4, Lolin_IR_Shield.D4
  N9: WeMos_D1_Mini_Relay_Shield_V1_PIN_D5.D8, Furnance_D8_Touch_Button.OUT
  N10: WeMos_D1_Mini_Relay_Shield_V1_PIN_D5.G, SSD1306_0_96"_OLED_Display_128x64_pixel.GND, 1000uf_capacitor.-
  N11: Lolin_IR_Shield.X3-Y8, IR1.GND
  N12: Lolin_IR_Shield.X4-Y8, IR1.Vs
  N13: Lolin_IR_Shield.X4-Y9, LED1.anode
  N14: Lolin_IR_Shield.X5-Y9, LED1.cathode
  N15: Lolin_IR_Shield.X6-Y8, IR1.Data

notes:
  Smartostat 5.0
  by Davide Perini

custom parts:
  HC-SR501 Body Sensor Module: Pyroelectric Infrared PIR Motion Sensor Detector Module
